# Fritzing sketch anahtar (saved by Fritzing 0.9.3b)
breadboards: 1

parts:
  Arduino1 = Arduino Mini (Rev5)
  S2 = Pushbutton [package="[THT]"]
  Parça1 = NRF24L01+ Breakout Board
  3_3V = Voltage Regulator LM1117 [package=sot223]
  C1 = Electrolytic Capacitor [capacitance=10µF package="100 mil [THT, electrolytic]"]

nets:
  GND: Arduino1.D2, Arduino1.GND, S2.Pin_1, S2.Pin_2, Parça1.GND, 3_3V.OUT, C1.-
  N1: Arduino1.D9_PWM, Parça1.CE
  N2: Arduino1.D13, Parça1.SCK
  N3: Arduino1.D12, Parça1.MISO
  N4: Arduino1.D11_PWM, Parça1.MOSI
  N5: Arduino1.D10_PWM, Parça1.CS
  N6: Arduino1.5V, 3_3V.ADJ
  N7: S2.Pin_3, S2.Pin_4
  N8: Parça1.VCC, 3_3V.IN, C1.+
